// Logisim project A2SM.circ as structural Verilog: 10 circuits, main circuit main
module main (
  input  [16:0] in_1,
  input  output_interrupt,
  input  input_interrupt
);

  wire and_1_out, clock_1_out, d_ff_1_q, Input_Flag_q, instruction_decoder_1_halt,
       instruction_decoder_1_input_flag_reset, instruction_decoder_1_iof, instruction_decoder_1_ion,
       instruction_decoder_1_reset_output_flag, Interrupt_q, Output_Flag_q;

  D_Flip_Flop Interrupt (
    .clk(and_1_out), .Q(Interrupt_q), .preset(instruction_decoder_1_ion), .reset(instruction_decoder_1_iof));  // open: D, Qn
  D_Flip_Flop Output_Flag (
    .D(output_interrupt), .clk(and_1_out), .Q(Output_Flag_q), .reset(instruction_decoder_1_reset_output_flag));  // open: Qn, preset
  Instruction_Decoder instruction_decoder_1 (
    .Clock(and_1_out), .I_flagQ(Interrupt_q), .Interrupt_Data(in_1), .FGI_in(Input_Flag_q),
    .FGO_in(Output_Flag_q), .reset_output_flag(instruction_decoder_1_reset_output_flag),
    .input_flag_reset(instruction_decoder_1_input_flag_reset), .IOF(instruction_decoder_1_iof),
    .Halt(instruction_decoder_1_halt), .ION(instruction_decoder_1_ion));
  D_Flip_Flop Input_Flag (
    .D(input_interrupt), .clk(and_1_out), .Q(Input_Flag_q), .reset(instruction_decoder_1_input_flag_reset));  // open: Qn, preset
  buf and_1 (and_1_out, clock_1_out);  // AND_Gate
  Clock clock_1 (.out(clock_1_out));
  D_Flip_Flop d_ff_1 (.clk(clock_1_out), .Q(d_ff_1_q), .reset(instruction_decoder_1_halt));  // open: D, Qn, preset
  POR por_1 (.out(d_ff_1_q));
endmodule

module register_bus (
  input  Select_SP,
  input  RAM_OUT,
  input  RAM_IN,
  input  AR_in,
  input  Clock,
  input  AR_out,
  input  PC_out,
  input  PC_INCREMENT,
  input  PC_In,
  input  IR_out,
  input  IR_in,
  input  reset_overflow_flag,
  input  A_out,
  input  B_in,
  input  A_in,
  input  [3:0] alu_operation,
  input  reset_A,
  input  [16:0] interrupt_input,
  input  INPTR_out,
  input  INPTR_in,
  input  OUTR_in,
  input  DR_out,
  input  E_complement,
  input  DR_inc,
  input  DR_in,
  input  SP_out,
  input  SP_dec,
  input  SP_inc,
  input  SP_IN,
  input  TR_in,
  input  TR_out,
  output [16:0] Instruction,
  output E,
  output [16:0] Accumulator_Value,
  output [16:0] interrupt_output,
  output [16:0] DR_output
);

  wire undriven, undriven_2;
  wire [16:0] AR_q, controlled_buffer_1_out, INPTR_q, multiplexer_1_out, PC_q, RAM_1_dout,
       stack_register_1_q, TR_q;

  Multiplexer #(.width(17)) multiplexer_1 (
    .in0(AR_q), .in1(stack_register_1_q), .out(multiplexer_1_out), .sel(Select_SP));
  Register #(.width(17)) INPTR (.D(interrupt_input), .en(INPTR_in), .clk(Clock), .Q(INPTR_q));  // open: clr
  Register #(.width(17)) OUTR (
    .D(controlled_buffer_1_out), .en(OUTR_in), .clk(Clock), .Q(interrupt_output));  // open: clr
  Register #(.width(17)) TR (.D(controlled_buffer_1_out), .en(TR_in), .clk(Clock), .Q(TR_q));  // open: clr
  Register #(.width(17)) IR (.D(controlled_buffer_1_out), .en(IR_in), .clk(Clock), .Q(Instruction));  // open: clr
  general_register AR (.D(controlled_buffer_1_out), .Load(AR_in), .Clock(Clock), .Q(AR_q));  // open: in_2, Inc, Reset
  general_register PC (
    .D(controlled_buffer_1_out), .Inc(PC_INCREMENT), .Load(PC_In), .Reset(undriven), .Clock(Clock), .Q(PC_q));  // open: in_2
  register_and_alu A (
    .Complement_E(E_complement), .RO(reset_overflow_flag), .Operation_Enable(B_in), .Loat_Enable(A_in),
    .D(controlled_buffer_1_out), .Clock(Clock), .B(controlled_buffer_1_out), .ops(alu_operation),
    .Reset_A(reset_A), .O(E), .Q(Accumulator_Value));
  general_register general_register_1 (
    .D(controlled_buffer_1_out), .Inc(DR_inc), .Load(DR_in), .Clock(Clock), .Q(DR_output));  // open: in_2, Reset
  RAM #(.addrWidth(13), .dataWidth(17)) RAM_1 (
    .addr(multiplexer_1_out[12:0]), .we(RAM_IN), .oe(1'b1), .clk(Clock), .din(controlled_buffer_1_out),
    .dout(RAM_1_dout));
  stack_register stack_register_1 (
    .D(controlled_buffer_1_out), .Dec(SP_dec), .Inc(SP_inc), .Load(SP_IN), .Reset(Clock),
    .Q(stack_register_1_q));  // open: in_2, Clock
  assign controlled_buffer_1_out = AR_out ? AR_q : 17'bz;  // Controlled_Buffer controlled_buffer_1
  assign controlled_buffer_1_out = PC_out ? PC_q : 17'bz;  // Controlled_Buffer controlled_buffer_2
  assign controlled_buffer_1_out = IR_out ? Instruction : 17'bz;  // Controlled_Buffer controlled_buffer_3
  assign controlled_buffer_1_out = A_out ? Accumulator_Value : 17'bz;  // Controlled_Buffer controlled_buffer_4
  assign controlled_buffer_1_out = INPTR_out ? INPTR_q : 17'bz;  // Controlled_Buffer controlled_buffer_5
  assign controlled_buffer_1_out = undriven_2 ? TR_q : 17'bz;  // Controlled_Buffer controlled_buffer_6
  assign controlled_buffer_1_out = RAM_OUT ? RAM_1_dout : 17'bz;  // Controlled_Buffer controlled_buffer_7
  assign controlled_buffer_1_out = DR_out ? DR_output : 17'bz;  // Controlled_Buffer controlled_buffer_8
  assign controlled_buffer_1_out = SP_out ? stack_register_1_q : 17'bz;  // Controlled_Buffer controlled_buffer_9
endmodule

module ALU (
  input  [3:0] ops,
  input  [16:0] B,
  input  C_in,
  input  [16:0] A,
  output Cout,
  output [16:0] alu_output
);

  wire arithmetic_circuit_1_cout, shift_circuit_1_c_out;
  wire [16:0] arithmetic_circuit_1_s, logical_circuit_1_output_bus_1, shift_circuit_1_shift_output;

  arithmetic_circuit arithmetic_circuit_1 (
    .Cin(C_in), .A(A), .B(B), .Ops(ops[1:0]), .S(arithmetic_circuit_1_s), .Cout(arithmetic_circuit_1_cout));
  logical_circuit logical_circuit_1 (.A(A), .B(B), .Ops(ops[1:0]), .Output_bus_1(logical_circuit_1_output_bus_1));
  shift_circuit shift_circuit_1 (
    .E(C_in), .A(A), .Ops(ops[0]), .shift_output(shift_circuit_1_shift_output), .C_out(shift_circuit_1_c_out));
  Multiplexer #(.select(2), .width(17)) multiplexer_1 (
    .in0(arithmetic_circuit_1_s), .in1(logical_circuit_1_output_bus_1), .in2(shift_circuit_1_shift_output),
    .in3(A), .out(alu_output), .sel(ops[3:2]));
  Multiplexer #(.select(2)) multiplexer_2 (
    .in0(arithmetic_circuit_1_cout), .in1(C_in), .in2(shift_circuit_1_c_out), .in3(C_in), .out(Cout),
    .sel(ops[3:2]));

  // Notes on the sheet:
  //   00 - arithmetic_circuit
  //   01 - Logical_circuit
  //   10 - shift_circuit
  //   11 - Transfer A
endmodule

module arithmetic_circuit (
  input  Cin,
  input  [16:0] A,
  input  [16:0] B,
  input  [1:0] Ops,
  output [16:0] S,
  output Cout
);

  wire and_1_out, decoder_1_out1;
  wire [16:0] multiplexer_1_out;

  Decoder #(.select(2)) decoder_1 (.out1(decoder_1_out1), .sel(Ops));  // open: out0, out2, out3, en
  Multiplexer #(.select(2), .width(17)) multiplexer_1 (
    .in0(B), .in1(B), .in2(17'h1), .in3({17{1'b1}}), .out(multiplexer_1_out), .sel(Ops));
  and and_1 (and_1_out, decoder_1_out1, Cin);
  Adder #(.width(17)) adder_1 (.a(A), .b(multiplexer_1_out), .out(S), .cin(and_1_out), .cout(Cout));

  // Notes on the sheet:
  //   11 - A - 1
  //   00- A + B
  //   01 - A + B + 1
  //   10 - A + 1
endmodule

module logical_circuit (
  input  [16:0] A,
  input  [16:0] B,
  input  [1:0] Ops,
  output [16:0] Output_bus_1
);

  wire [16:0] and_1_out, not_1_out, or_1_out, xor_1_out;

  assign and_1_out = A & B;  // AND_Gate and_1, 17 bits wide
  assign or_1_out = A | B;  // OR_Gate or_1, 17 bits wide
  assign not_1_out = ~A;  // NOT_Gate not_1, 17 bits wide
  assign xor_1_out = A ^ B;  // XOR_Gate xor_1, 17 bits wide
  Multiplexer #(.select(2), .width(17)) multiplexer_1 (
    .in0(and_1_out), .in1(or_1_out), .in2(xor_1_out), .in3(not_1_out), .out(Output_bus_1), .sel(Ops));

  // Notes on the sheet:
  //   00 - A and B
  //   01 - A or B
  //   10 - A xor B
  //   11 - not A
endmodule

module shift_circuit (
  input  E,
  input  [16:0] A,
  input  Ops,
  output [16:0] shift_output,
  output C_out
);

  Multiplexer #(.width(17)) multiplexer_1 (.in0({E, A[16:1]}), .in1({A[15:0], E}), .out(shift_output), .sel(Ops));
  Multiplexer multiplexer_2 (.in0(A[0]), .in1(A[16]), .out(C_out), .sel(Ops));

  // Notes on the sheet:
  //   0-shift right
  //   1-shift left
endmodule

module general_register (
  input  [16:0] D,
  input  [3:0] in_2,
  input  Inc,
  input  Load,
  input  Reset,
  input  Clock,
  output [16:0] Q
);

  wire xor_1_out;
  wire [12:0] adder_1_out, multiplexer_1_out;

  Multiplexer #(.width(13)) multiplexer_1 (.in0(D[12:0]), .in1(adder_1_out), .out(multiplexer_1_out), .sel(Inc));
  xor xor_1 (xor_1_out, Inc, Load);
  Register #(.width(13)) register_1 (.D(multiplexer_1_out), .en(xor_1_out), .clk(Clock), .Q(Q[12:0]), .clr(Reset));
  Adder #(.width(13)) adder_1 (.a(Q[12:0]), .b(13'h1), .out(adder_1_out));  // open: cin, cout

  assign Q[16:13] = 4'b0000;
endmodule

module register_and_alu (
  input  Complement_E,
  input  RO,
  input  Operation_Enable,
  input  Loat_Enable,
  input  [16:0] D,
  input  Clock,
  input  [16:0] B,
  input  [3:0] ops,
  input  Reset_A,
  output O,
  output [16:0] Q
);

  wire main_alu_cout, multiplexer_1_out, not_1_out, or_1_out;
  wire [16:0] register_1_q;

  or or_1 (or_1_out, Operation_Enable, Complement_E);
  Register #(.width(17)) register_1 (.D(D), .en(Loat_Enable), .clk(Clock), .Q(register_1_q), .clr(Reset_A));
  not not_1 (not_1_out, O);
  Multiplexer multiplexer_1 (.in0(main_alu_cout), .in1(not_1_out), .out(multiplexer_1_out), .sel(Complement_E));
  Register #(.width(1)) overflow (.D(multiplexer_1_out), .en(or_1_out), .clk(Clock), .Q(O), .clr(RO));
  ALU main_alu (.ops(ops), .B(B), .C_in(O), .A(register_1_q), .Cout(main_alu_cout), .alu_output(Q));
endmodule

module Instruction_Decoder (
  input  Clock,
  input  I_flagQ,
  input  [16:0] Interrupt_Data,
  input  FGI_in,
  input  FGO_in,
  output reset_output_flag,
  output input_flag_reset,
  output IOF,
  output Halt,
  output ION
);

  wire A_clear, AI, Ain, and_1_out, and_3_out, and_5_out, and_7_out, and_10_out, and_12_out, and_13_out,
       and_14_out, and_15_out, and_19_out, and_21_out, and_22_out, and_23_out, and_24_out, and_25_out,
       and_26_out, and_27_out, and_28_out, and_29_out, and_30_out, and_31_out, and_32_out, and_33_out,
       and_34_out, and_35_out, and_36_out, and_37_out, and_38_out, and_39_out, and_40_out, and_41_out,
       and_42_out, and_43_out, and_44_out, and_45_out, and_46_out, and_47_out, and_48_out, and_49_out,
       and_50_out, and_51_out, and_52_out, and_53_out, and_54_out, and_55_out, and_56_out, and_57_out,
       and_58_out, and_59_out, and_60_out, and_61_out, and_62_out, AO, Aout, B0, B1, B2, B3, B4, B5, B6, B7,
       B8, B9, B10, B11, B12, bcd_to_7_segment_decoder_1_p1, Bin, binary_to_bcd_converter_1_p3, BO,
       comparator_1_eq, comparator_1_gt, comparator_1_lt, comparator_2_eq, D0, D1, D2, D3, D4, D5, D6, D7,
       decoder_2_out7, DI, DInc, DO, E_Com, EC, I, nand_1_out, not_1_out, not_2_out, not_3_out, not_4_out,
       not_5_out, not_6_out, not_7_out, not_8_out, not_9_out, not_10_out, not_11_out, not_12_out, not_13_out,
       not_14_out, not_15_out, not_16_out, not_17_out, not_18_out, not_19_out, not_20_out, not_21_out,
       not_22_out, or_1_out, or_2_out, or_4_out, or_6_out, or_7_out, or_8_out, or_11_out, or_12_out,
       or_13_out, or_14_out, or_15_out, or_16_out, or_17_out, or_18_out, or_21_out, or_24_out, or_28_out,
       or_29_out, or_30_out, Overflow, P_inc, PI, PO, RI, RO, SD, SI, SPS, T0, T1, T2, T3, T4, T5, T6,
       undriven;
  wire [3:0] counter_1_q, Op;
  wire [15:13] register_bus_1_instruction;
  wire [16:0] AC, DR, Interrupt_out;

  or or_1 (or_1_out, D0, D3, D6);
  and and_1 (and_1_out, D1, T6);
  and and_2 (DInc, D1, T5);
  not not_1 (not_1_out, I);
  and and_3 (and_3_out, D1, T6);
  or or_2 (or_2_out, D0, D1, D5, D6);
  and and_4 (reset_output_flag, D7, I, B5, T3);
  and and_5 (and_5_out, T5, or_1_out);
  or or_3 (DO, and_5_out, and_1_out);
  and and_6 (E_Com, D7, not_1_out, B10, T3);
  and and_7 (and_7_out, or_2_out, T4);
  and and_8 (IOF, D7, I, B1, T3);
  Counter #(.max('hf), .width(4)) counter_1 (
    .clr(decoder_2_out7), .clk(Clock), .Q(counter_1_q));  // open: load, up, count, D, carry
  and and_9 (ION, D7, I, BO, T3);
  or or_4 (or_4_out, B8, B3, B7);
  or or_5 (DI, and_3_out, and_7_out);
  not not_2 (not_2_out, I);
  not not_3 (not_3_out, I);
  or or_6 (or_6_out, D0, D6);
  and and_10 (and_10_out, T5, or_6_out);
  or or_7 (or_7_out, B9, B7, B5);
  and and_11 (Halt, D7, not_3_out, B1, T3);
  and and_12 (and_12_out, D2, T4);
  and and_13 (and_13_out, D7, not_2_out, or_4_out, T3);
  _7_Segment_Display u_7_segment_display_1 ();  // open: g, f, a, b, e, d, c, dp
  // BCD_to_7_Segment_decoder bcd_to_7_segment_decoder_1: pin names not known; wires that end beside it: bcd_to_7_segment_decoder_1_p1
  // Binary_to_BCD_converter #(.binvalue(4)) binary_to_bcd_converter_1: pin names not known; wires that end beside it: counter_1_q, bcd_to_7_segment_decoder_1_p1, binary_to_bcd_converter_1_p3
  or or_8 (or_8_out, D0, D3, D6);
  not not_4 (not_4_out, I);
  _7_Segment_Display u_7_segment_display_2 ();  // open: g, f, a, b, e, d, c, dp
  // BCD_to_7_Segment_decoder bcd_to_7_segment_decoder_2: pin names not known; wires that end beside it: binary_to_bcd_converter_1_p3
  and and_14 (and_14_out, T5, or_8_out);
  and and_15 (and_15_out, D7, not_4_out, or_7_out, T3);
  not not_5 (not_5_out, I);
  or or_9 (Aout, and_12_out, and_13_out, and_10_out);
  and and_16 (input_flag_reset, D7, I, B4, T3);
  and and_17 (SI, D4, T4);
  or or_10 (Ain, input_flag_reset, and_14_out, and_15_out);
  and and_18 (SD, D7, not_5_out, B0, T3);
  register_bus register_bus_1 (
    .Select_SP(SPS), .RAM_OUT(RO), .RAM_IN(RI), .AR_in(AI), .Clock(Clock), .AR_out(AO), .PC_out(PO),
    .PC_INCREMENT(P_inc), .PC_In(PI), .IR_out(T2), .IR_in(T1), .reset_overflow_flag(EC), .A_out(Aout),
    .B_in(Bin), .A_in(Ain), .alu_operation(Op), .reset_A(A_clear), .interrupt_input(Interrupt_Data),
    .INPTR_out(input_flag_reset), .INPTR_in(I_flagQ), .OUTR_in(reset_output_flag), .DR_out(DO),
    .E_complement(E_Com), .DR_inc(DInc), .DR_in(DI), .SP_out(1'b0), .SP_dec(SI), .SP_inc(SD), .SP_IN(1'b0),
    .TR_in(1'b1), .TR_out(1'b0),
    .Instruction({I, register_bus_1_instruction, B12, B11, B10, B9, B8, B7, B6, B5, B4, B3, B2, B1, B0}),
    .E(Overflow), .Accumulator_Value(AC), .interrupt_output(Interrupt_out), .DR_output(DR));
  and and_19 (and_19_out, D0, D6);
  and and_20 (Bin, T5, and_19_out);
  Decoder #(.select(3)) decoder_1 (
    .out0(D0), .out1(D1), .out2(D2), .out3(D3), .out4(D4), .out5(D5), .out6(D6), .out7(D7),
    .sel(register_bus_1_instruction));  // open: en
  Decoder #(.select(4)) decoder_2 (
    .out0(T0), .out1(T1), .out2(T2), .out3(T3), .out4(T4), .out5(T5), .out6(T6), .out7(decoder_2_out7),
    .sel(counter_1_q), .en(undriven));  // open: out8, out9, out10, out11, out12, out13, out14, out15
  not not_6 (not_6_out, I);
  or or_11 (or_11_out, B8, B9);
  or or_12 (or_12_out, B5, B9);
  or or_13 (or_13_out, D0, D6);
  or or_14 (or_14_out, B5, B7, B8);
  not not_7 (not_7_out, I);
  not not_8 (not_8_out, I);
  or or_15 (or_15_out, B5, B9);
  and and_21 (and_21_out, D7, not_6_out, B5, T3);
  nand nand_1 (nand_1_out, T5, or_13_out);
  not not_9 (not_9_out, I);
  not not_10 (not_10_out, I);
  not not_11 (not_11_out, I);
  and and_22 (and_22_out, D6, T5);
  or or_16 (or_16_out, B7, B8);
  and and_23 (and_23_out, D0, T5);
  and and_24 (and_24_out, D7, not_7_out, or_11_out, T3);
  and and_25 (and_25_out, D7, not_8_out, or_12_out, T3);
  and and_26 (and_26_out, D7, not_9_out, or_14_out, T3);
  and and_27 (and_27_out, D6, T5);
  and and_28 (and_28_out, D2, T4);
  and and_29 (and_29_out, D0, T5);
  not not_12 (not_12_out, I);
  or or_17 (or_17_out, and_23_out, and_21_out);
  and and_30 (and_30_out, D6, T5);
  and and_31 (and_31_out, D7, not_10_out, B9, T3);
  and and_32 (and_32_out, D7, not_11_out, or_15_out, T3);
  and and_33 (and_33_out, D0, T5);
  not not_13 (not_13_out, or_17_out);
  or or_18 (or_18_out, and_30_out, and_24_out);
  and and_34 (and_34_out, D0, T5);
  and and_35 (and_35_out, D7, not_12_out, or_16_out, T3);
  or or_19 (Op[1], and_25_out, nand_1_out);
  and and_36 (and_36_out, and_31_out, and_27_out, and_28_out);
  and and_37 (and_37_out, and_32_out, and_29_out, and_22_out);
  not not_14 (not_14_out, and_37_out);
  not not_15 (not_15_out, I);
  or or_20 (Op[0], not_13_out, or_18_out);
  or or_21 (or_21_out, and_26_out, and_34_out);
  not not_16 (not_16_out, or_21_out);
  and and_38 (and_38_out, and_35_out, and_33_out);
  and and_39 (and_39_out, D4, T4);
  and and_40 (and_40_out, D7, not_15_out, B0, T5);
  or or_22 (Op[2], not_16_out, and_36_out);
  or or_23 (Op[3], not_14_out, and_38_out);
  or or_24 (or_24_out, D4, D0, D1, D3, D6);
  and and_41 (and_41_out, D4, T5);
  and and_42 (and_42_out, D5, T4);
  or or_25 (SPS, and_39_out, and_40_out);
  and and_43 (and_43_out, T4, or_24_out);
  not not_17 (not_17_out, I);
  not not_18 (not_18_out, Overflow);
  Comparator #(.width(17)) comparator_1 (
    .a(AC), .b({17{1'b0}}), .gt(comparator_1_gt), .eq(comparator_1_eq), .lt(comparator_1_lt));
  or or_26 (RO, T1, and_43_out);
  or or_27 (AO, and_41_out, and_42_out);
  and and_44 (and_44_out, B2, FGI_in);
  and and_45 (and_45_out, B3, FGO_in);
  and and_46 (and_46_out, B6, comparator_1_gt);
  and and_47 (and_47_out, B3, comparator_1_lt);
  and and_48 (and_48_out, not_18_out, B1);
  and and_49 (and_49_out, comparator_1_eq, B4);
  not not_19 (not_19_out, D7);
  or or_28 (or_28_out, and_44_out, and_45_out);
  and and_50 (and_50_out, not_19_out, I, T3);
  and and_51 (and_51_out, I, or_28_out);
  or or_29 (or_29_out, and_46_out, and_49_out, and_47_out, and_48_out);
  and and_52 (and_52_out, not_17_out, or_29_out);
  Comparator #(.width(17)) comparator_2 (.a(DR), .b({17{1'b0}}), .eq(comparator_2_eq));  // open: gt, lt
  and and_53 (and_53_out, D7, I, B0, T5);
  or or_30 (or_30_out, and_51_out, and_52_out);
  and and_54 (and_54_out, D7, T3);
  or or_31 (AI, T2, T0, and_50_out);
  and and_55 (and_55_out, or_30_out, and_54_out);
  and and_56 (and_56_out, comparator_2_eq, D1, T6);
  and and_57 (and_57_out, T6, D6);
  and and_58 (and_58_out, T4, D2);
  or or_32 (P_inc, and_55_out, T1, and_56_out);
  not not_20 (not_20_out, I);
  and and_59 (and_59_out, D4, T5);
  and and_60 (and_60_out, D5, T4);
  and and_61 (and_61_out, D4, T4);
  not not_21 (not_21_out, I);
  or or_33 (RI, and_58_out, and_57_out, and_53_out);
  and and_62 (and_62_out, D7, not_20_out, B0, T5);
  and and_63 (EC, D7, not_21_out, B10, T3);
  or or_34 (PO, and_61_out, T0);
  or or_35 (PI, and_59_out, and_62_out, and_60_out);
  not not_22 (not_22_out, I);
  and and_64 (A_clear, D7, not_22_out, B11, T3);

  // Other names for the same wires on the sheet: INO = input_flag_reset; input_flag_in = FGI_in;
  //   ONI = reset_output_flag; output_flag_in = FGO_in
endmodule

module stack_register (
  input  [16:0] D,
  input  [3:0] in_2,
  input  Dec,
  input  Inc,
  input  Load,
  input  Reset,
  input  Clock,
  output [16:0] Q
);

  wire xor_1_out;
  wire [12:0] adder_1_out, multiplexer_1_out, multiplexer_2_out;

  Multiplexer #(.width(13)) multiplexer_1 (.in0(D[12:0]), .in1(adder_1_out), .out(multiplexer_1_out), .sel(Dec));
  ExactlyOne xor_1 (.out(xor_1_out), .in0(Dec), .in1(Inc), .in2(Load));
  Register #(.width(13)) register_1 (.D(multiplexer_1_out), .en(xor_1_out), .clk(Clock), .Q(Q[12:0]), .clr(Reset));
  Multiplexer #(.width(13)) multiplexer_2 (.in0({13{1'b1}}), .in1(13'h1), .out(multiplexer_2_out), .sel(Inc));
  Adder #(.width(13)) adder_1 (.a(Q[12:0]), .b(multiplexer_2_out), .out(adder_1_out));  // open: cin, cout

  assign Q[16:13] = in_2;
endmodule
